// Logisim project Lab_6_MAngle.circ as structural Verilog: 14 circuits, main circuit main
module main (
  input  Ena,
  input  Clear
);

  wire b0, b1, b2, b3, b4, b5, b6, c0, c1, c2, c3, c4, c5, c6, Clk_out;
  wire [3:0] SyncDwnCnt10_Ena_Clr_1_count;
  wire [7:7] Bin2Hex_1_hex0, Bin2Hex_1_hex1;

  Clock Clk (.out(Clk_out));
  SyncDwnCnt10_Ena_Clr SyncDwnCnt10_Ena_Clr_1 (
    .Clear(Clear), .Enable(Ena), .Clock(Clk_out), .Count(SyncDwnCnt10_Ena_Clr_1_count));
  _7_Segment_Display #(.active("false")) L_7_Segment_Display_3 (
    .g(b6), .f(b5), .a(b0), .b(b1), .e(b4), .d(b3), .c(b2), .dp(1'b1));
  _7_Segment_Display #(.active("false")) L_7_Segment_Display_4 (
    .g(c6), .f(c5), .a(c0), .b(c1), .e(c4), .d(c3), .c(c2), .dp(1'b1));
  Bin2Hex Bin2Hex_1 (
    .v3(SyncDwnCnt10_Ena_Clr_1_count[3]), .v2(SyncDwnCnt10_Ena_Clr_1_count[2]),
    .v1(SyncDwnCnt10_Ena_Clr_1_count[1]), .v0(SyncDwnCnt10_Ena_Clr_1_count[0]),
    .HEX1({Bin2Hex_1_hex1[7], b6, b5, b4, b3, b2, b1, b0}),
    .HEX0({Bin2Hex_1_hex0[7], c6, c5, c4, c3, c2, c1, c0}));

  // Notes on the sheet:
  //   Counter Display
endmodule

module Seg7_Decoder (
  input  i_m3,
  input  i_m2,
  input  i_m1,
  input  i_m0,
  output [7:0] o_seg
);

  wire and_1_out, and_2_out, and_3_out, and_4_out, and_5_out, and_6_out, and_7_out, and_8_out, and_9_out,
       and_10_out, and_11_out, and_12_out, and_13_out, and_14_out, and_15_out, and_16_out, and_17_out,
       and_18_out, and_19_out, and_20_out, and_21_out, and_22_out, and_23_out, not_1_out, not_2_out,
       not_3_out, not_4_out;

  not not_1 (not_1_out, i_m3);
  not not_2 (not_2_out, i_m2);
  not not_3 (not_3_out, i_m1);
  not not_4 (not_4_out, i_m0);
  and and_1 (and_1_out, not_1_out, not_2_out, not_3_out);
  and and_2 (and_2_out, not_1_out, i_m2, i_m1, i_m0);
  and and_3 (and_3_out, i_m3, not_2_out, i_m1);
  and and_4 (and_4_out, not_1_out, not_2_out, i_m0);
  and and_5 (and_5_out, not_1_out, not_2_out, i_m1);
  and and_6 (and_6_out, not_2_out, i_m1, i_m0);
  and and_7 (and_7_out, i_m3, i_m2, not_3_out);
  and and_8 (and_8_out, not_1_out, i_m2, not_3_out);
  and and_9 (and_9_out, i_m3, i_m2, i_m1);
  and and_10 (and_10_out, not_1_out, not_2_out, not_3_out, i_m0);
  and and_11 (and_11_out, not_1_out, i_m2, not_3_out, not_4_out);
  and and_12 (and_12_out, not_1_out, i_m2, i_m1, i_m0);
  and and_13 (and_13_out, i_m3, not_2_out, i_m1, i_m0);
  and and_14 (and_14_out, i_m3, i_m2, i_m1, not_4_out);
  and and_15 (and_15_out, not_1_out, not_2_out, i_m1, not_4_out);
  and and_16 (and_16_out, i_m3, i_m2, not_3_out, not_4_out);
  and and_17 (and_17_out, not_1_out, i_m2, not_3_out, i_m0);
  and and_18 (and_18_out, not_1_out, i_m2, i_m1, not_4_out);
  and and_19 (and_19_out, i_m3, i_m2, i_m1, i_m0);
  and and_20 (and_20_out, not_1_out, not_2_out, not_3_out, i_m0);
  and and_21 (and_21_out, not_1_out, i_m2, not_3_out, not_4_out);
  and and_22 (and_22_out, i_m3, not_2_out, i_m1, i_m0);
  and and_23 (and_23_out, i_m3, i_m2, i_m1, not_4_out);
  or or_1 (o_seg[6], and_1_out, and_2_out, and_3_out);
  or or_2 (o_seg[5], and_4_out, and_5_out, and_6_out, and_7_out);
  or or_3 (o_seg[4], i_m0, and_8_out, and_9_out);
  or or_4 (o_seg[3], and_10_out, and_11_out, and_12_out, and_13_out, and_14_out);
  or or_5 (o_seg[2], and_15_out, and_16_out);
  or or_6 (o_seg[1], and_17_out, and_18_out, and_19_out);
  or or_7 (o_seg[0], and_20_out, and_21_out, and_22_out, and_23_out);

  assign o_seg[7] = 1'b1;
endmodule

module CircuitA (
  input  i2,
  input  i1,
  input  i0,
  output o2,
  output o1,
  output o0
);

  not not_1 (o1, i1);
  and and_1 (o2, i2, i1);

  assign o0 = i0;
endmodule

module myComparator (
  input  v3,
  input  v2,
  input  v1,
  input  v0,
  output z
);

  wire and_1_out, and_2_out;

  and and_1 (and_1_out, v3, v1);
  and and_2 (and_2_out, v3, v2);
  or or_1 (z, and_1_out, and_2_out);
endmodule

module CircuitB (
  input  z,
  output s6,
  output s5,
  output s4,
  output s3,
  output s2,
  output s1,
  output s0
);


  assign s0 = z;
  assign s1 = 1'b0;
  assign s2 = 1'b0;
  assign s3 = z;
  assign s4 = z;
  assign s5 = z;
  assign s6 = 1'b1;
endmodule

module Bin2Hex (
  input  v3,
  input  v2,
  input  v1,
  input  v0,
  output [7:0] HEX1,
  output [7:0] HEX0
);

  wire z;

  myComparator myComparator_1 (.v3(v3), .v2(v2), .v1(v1), .v0(v0), .z(z));
  CircuitB CircuitB_1 (
    .z(z), .s6(HEX1[6]), .s5(HEX1[5]), .s4(HEX1[4]), .s3(HEX1[3]), .s2(HEX1[2]), .s1(HEX1[1]), .s0(HEX1[0]));
  Seg7_Decoder Seg7_Decoder_1 (.i_m3(v3), .i_m2(v2), .i_m1(v1), .i_m0(v0), .o_seg(HEX0));

  assign HEX1[7] = 1'b1;
endmodule

module UpCounter_Template (
  input  en,
  input  Clock,
  output [3:0] Count
);

  wire t_ff_1_qn, t_ff_2_qn, t_ff_3_qn;

  T_Flip_Flop t_ff_1 (.T(en), .clk(Clock), .Q(Count[0]), .Qn(t_ff_1_qn));  // open: reset, preset
  T_Flip_Flop t_ff_2 (.T(en), .clk(t_ff_1_qn), .Q(Count[1]), .Qn(t_ff_2_qn));  // open: reset, preset
  T_Flip_Flop t_ff_3 (.T(en), .clk(t_ff_2_qn), .Q(Count[2]), .Qn(t_ff_3_qn));  // open: reset, preset
  T_Flip_Flop t_ff_4 (.T(en), .clk(t_ff_3_qn), .Q(Count[3]));  // open: Qn, reset, preset
endmodule

module DownCounter_Template (
  input  en,
  input  Clock,
  output [3:0] Count
);

  T_Flip_Flop t_ff_1 (.T(en), .clk(Clock), .Q(Count[0]));  // open: Qn, reset, preset
  T_Flip_Flop t_ff_2 (.T(en), .clk(Count[0]), .Q(Count[1]));  // open: Qn, reset, preset
  T_Flip_Flop t_ff_3 (.T(en), .clk(Count[1]), .Q(Count[2]));  // open: Qn, reset, preset
  T_Flip_Flop t_ff_4 (.T(en), .clk(Count[2]), .Q(Count[3]));  // open: Qn, reset, preset
endmodule

module Mod5_Template (
  input  Enable,
  input  Clock
);

  wire and_1_out, nand_1_out, not_1_out, not_2_out, not_3_out, t_ff_1_q, t_ff_2_q, t_ff_3_q;

  T_Flip_Flop t_ff_1 (.T(Enable), .clk(Clock), .Q(t_ff_1_q), .reset(not_1_out));  // open: Qn, preset
  not not_1 (not_1_out, nand_1_out);
  T_Flip_Flop t_ff_2 (.T(t_ff_1_q), .clk(Clock), .Q(t_ff_2_q), .reset(not_2_out));  // open: Qn, preset
  not not_2 (not_2_out, nand_1_out);
  and and_1 (and_1_out, t_ff_1_q, t_ff_2_q);
  T_Flip_Flop t_ff_3 (.T(and_1_out), .clk(Clock), .Q(t_ff_3_q), .reset(not_3_out));  // open: Qn, preset
  not not_3 (not_3_out, nand_1_out);
  nand nand_1 (nand_1_out, t_ff_1_q, t_ff_3_q);
endmodule

module Johnson_Counter_Template (
  input  Clock,
  input  Reset,
  output [3:0] Count
);

  wire not_1_out, not_2_out, not_3_out, not_4_out, t_ff_4_qn;

  T_Flip_Flop t_ff_1 (.T(t_ff_4_qn), .clk(Clock), .Q(Count[0]), .reset(not_1_out));  // open: Qn, preset
  not not_1 (not_1_out, Reset);
  T_Flip_Flop t_ff_2 (.T(Count[0]), .clk(Clock), .Q(Count[1]), .reset(not_2_out));  // open: Qn, preset
  not not_2 (not_2_out, Reset);
  T_Flip_Flop t_ff_3 (.T(Count[1]), .clk(Clock), .Q(Count[2]), .reset(not_3_out));  // open: Qn, preset
  not not_3 (not_3_out, Reset);
  T_Flip_Flop t_ff_4 (.T(Count[2]), .clk(Clock), .Q(Count[3]), .Qn(t_ff_4_qn), .reset(not_4_out));  // open: preset
  not not_4 (not_4_out, Reset);
endmodule

module UpCounter_Ena_Clr (
  input  Enable,
  input  Clock,
  input  Clear,
  output [3:0] Count
);

  wire and_1_out, and_2_out, and_3_out;

  T_Flip_Flop t_ff_1 (.T(Enable), .clk(Clock), .Q(Count[0]), .reset(Clear));  // open: Qn, preset
  and and_1 (and_1_out, Enable, Count[0]);
  T_Flip_Flop t_ff_2 (.T(and_1_out), .clk(Clock), .Q(Count[1]), .reset(Clear));  // open: Qn, preset
  and and_2 (and_2_out, and_1_out, Count[1]);
  T_Flip_Flop t_ff_3 (.T(and_2_out), .clk(Clock), .Q(Count[2]), .reset(Clear));  // open: Qn, preset
  and and_3 (and_3_out, and_2_out, Count[2]);
  T_Flip_Flop t_ff_4 (.T(and_3_out), .clk(Clock), .Q(Count[3]), .reset(Clear));  // open: Qn, preset
endmodule

module DownCounter_Ena_Clr (
  input  Enable,
  input  Clock,
  input  Clear,
  output [3:0] Count
);

  wire not_1_out, not_2_out, not_3_out, not_4_out;

  T_Flip_Flop t_ff_1 (.T(Enable), .clk(Clock), .Q(Count[0]), .reset(not_1_out));  // open: Qn, preset
  not not_1 (not_1_out, Clear);
  T_Flip_Flop t_ff_2 (.T(Enable), .clk(Count[0]), .Q(Count[1]), .reset(not_2_out));  // open: Qn, preset
  not not_2 (not_2_out, Clear);
  T_Flip_Flop t_ff_3 (.T(Enable), .clk(Count[1]), .Q(Count[2]), .reset(not_3_out));  // open: Qn, preset
  not not_3 (not_3_out, Clear);
  T_Flip_Flop t_ff_4 (.T(Enable), .clk(Count[2]), .Q(Count[3]), .reset(not_4_out));  // open: Qn, preset
  not not_4 (not_4_out, Clear);
endmodule

module DownCnt10_Ena_Clr (
  input  Clear,
  input  Enable,
  input  Clock,
  output [3:0] Count
);

  wire nor_1_out, not_1_out, not_2_out, not_3_out, not_4_out, or_1_out, undriven;

  T_Flip_Flop t_ff_1 (.T(Enable), .clk(or_1_out), .Q(Count[0]), .reset(not_1_out));  // open: Qn, preset
  or or_1 (or_1_out, Clock, nor_1_out);
  not not_1 (not_1_out, Clear);
  not not_2 (not_2_out, Clear);
  T_Flip_Flop t_ff_2 (.T(Enable), .clk(Count[0]), .Q(Count[1]), .reset(undriven), .preset(not_2_out));  // open: Qn
  T_Flip_Flop t_ff_3 (.T(Enable), .clk(Count[1]), .Q(Count[2]), .reset(not_3_out));  // open: Qn, preset
  not not_3 (not_3_out, Clear);
  T_Flip_Flop t_ff_4 (.T(Enable), .clk(Count[2]), .Q(Count[3]), .preset(not_4_out));  // open: Qn, reset
  not not_4 (not_4_out, Clear);
  nor nor_1 (nor_1_out, Count[0], Count[1], Count[2], Count[3]);
endmodule

module SyncDwnCnt10_Ena_Clr (
  input  Clear,
  input  Enable,
  input  Clock,
  output [3:0] Count
);

  wire and_2_out, and_3_out, Clear_t, nor_1_out, not_1_out, not_2_out, not_3_out, not_4_out, or_1_out,
       t_ff_1_qn, t_ff_2_qn, t_ff_3_qn;

  or or_1 (or_1_out, Clock, nor_1_out);
  and and_1 (Clear_t, Clear, Enable);
  T_Flip_Flop t_ff_1 (.T(Enable), .clk(or_1_out), .Q(Count[0]), .Qn(t_ff_1_qn), .reset(not_1_out));  // open: preset
  not not_1 (not_1_out, Clear_t);
  not not_2 (not_2_out, Clear_t);
  T_Flip_Flop t_ff_2 (.T(t_ff_1_qn), .clk(or_1_out), .Q(Count[1]), .Qn(t_ff_2_qn), .preset(not_2_out));  // open: reset
  and and_2 (and_2_out, t_ff_1_qn, t_ff_2_qn);
  T_Flip_Flop t_ff_3 (.T(and_2_out), .clk(or_1_out), .Q(Count[2]), .Qn(t_ff_3_qn), .reset(not_3_out));  // open: preset
  not not_3 (not_3_out, Clear_t);
  and and_3 (and_3_out, and_2_out, t_ff_3_qn);
  T_Flip_Flop t_ff_4 (.T(and_3_out), .clk(or_1_out), .Q(Count[3]), .preset(not_4_out));  // open: Qn, reset
  not not_4 (not_4_out, Clear_t);
  nor nor_1 (nor_1_out, Count[0], Count[1], Count[2], Count[3]);
endmodule
